// Logisim project processor (suprise).circ as structural Verilog
module ALU (
  input  [2:0] F,
  input  [31:0] B,
  input  [31:0] A,
  output [31:0] Y,
  output ZERO
);

  wire [31:0] A___B_2_out, A___B_out, adder_1_out, bit_extender_1_out, multiplexer_1_out, multiplexer_2_out,
       multiplier_1_out, not_1_out;
  wire [31:1] nor_1_out;

  assign not_1_out = ~B;  // NOT_Gate not_1, 32 bits wide
  Multiplexer #(.width(32), .enable("false")) multiplexer_1 (
    .in0(B), .in1(not_1_out), .out(multiplexer_1_out), .sel(F[2]));
  Multiplier #(.width(32)) multiplier_1 (.a(multiplexer_1_out), .b(A), .out(multiplier_1_out));  // open: cin, cout
  Adder #(.width(32)) adder_1 (.a(multiplexer_1_out), .b(A), .out(adder_1_out), .cin(F[2]));  // open: cout
  assign A___B_out = multiplexer_1_out & A;  // AND_Gate A___B, 32 bits wide
  assign A___B_2_out = multiplexer_1_out | A;  // OR_Gate A___B_2, 32 bits wide
  assign bit_extender_1_out = {{31{1'b0}}, adder_1_out[31]};  // Bit_Extender bit_extender_1
  Multiplexer #(.width(32), .enable("false")) multiplexer_2 (
    .in0(multiplier_1_out), .in1(bit_extender_1_out), .out(multiplexer_2_out), .sel(F[2]));
  Multiplexer #(.select(2), .width(32), .enable("false")) multiplexer_3 (
    .in0(A___B_out), .in1(A___B_2_out), .in2(adder_1_out), .in3(multiplexer_2_out), .out(Y), .sel(F[1:0]));
  assign {nor_1_out, ZERO} = ~(Y | {32{1'b0}});  // NOR_Gate nor_1, 32 bits wide

  // Notes on the sheet:
  //   Control bits
  //   During add the control bit is carry in
  //   due to sub using 2's complement
  //   Shift left 31 bits
  //   Comparator outputs 1 or zero depending on what type of comparison is made
  //   ALU
  //   funktion
  //   F2
  //   000     A AND B
  //   001      A  OR B
  //   010     A     + B
  //   011   NOT USED
  //   100     A AND !B
  //   101     A OR !B
  //   110     A - B
  //   111     SLT
endmodule

module Datapath (
  output [31:0] Data_Memory,
  output [31:0] v0
);

  wire alu_1_zero, and_1_out, clock_1_out, controlunit_1_alusrc, controlunit_1_branch, controlunit_1_regdst,
       controlunit_1_regwrite;
  wire [2:0] controlunit_1_alucontrol, multiplexer_2_out;
  wire [7:0] adder_1_out, adder_2_out, bitselector_2_out, multiplexer_1_out, register_1_q, shifter_1_out,
       shifter_2_out;
  wire [15:0] bitselector_1_out;
  wire [31:0] bit_extender_1_out, multiplexer_3_out, registerfile_1_rd1, registerfile_1_rd2, rom_1_data;

  Clock clock_1 (.out(clock_1_out));
  Multiplexer #(.width(8), .enable("false")) multiplexer_1 (
    .in0(adder_1_out), .in1(adder_2_out), .out(multiplexer_1_out), .sel(and_1_out));
  Register #(.Select("low")) register_1 (.D(multiplexer_1_out), .Q(register_1_q), .clk(clock_1_out));  // open: en, clr
  Shifter #(.shift("lr")) shifter_1 (.in(register_1_q), .\dist (3'b010), .out(shifter_1_out));
  Adder adder_1 (.a(register_1_q), .b(8'h4), .out(adder_1_out));  // open: cin, cout
  ROM #(.dataWidth(32), .Select("high")) rom_1 (.addr(shifter_1_out), .data(rom_1_data));
  BitSelector #(.width(32), .group(16)) bitselector_1 (.in(rom_1_data), .out(bitselector_1_out), .sel(1'b0));
  ControlUnit controlunit_1 (
    .Instruction(rom_1_data), .RegDst(controlunit_1_regdst), .RegWrite(controlunit_1_regwrite),
    .ALUControl(controlunit_1_alucontrol), .Branch(controlunit_1_branch), .ALUSrc(controlunit_1_alusrc));
  assign bit_extender_1_out = {{16{bitselector_1_out[15]}}, bitselector_1_out};  // Bit_Extender bit_extender_1
  RegisterFile registerfile_1 (
    .CLK(clock_1_out), .A1(rom_1_data[23:21]), .WD3(Data_Memory), .A2(rom_1_data[18:16]),
    .WE3(controlunit_1_regwrite), .RD1(registerfile_1_rd1), .RD2(registerfile_1_rd2), .A3(multiplexer_2_out),
    .V0(v0));
  Multiplexer #(.width(3), .enable("false")) multiplexer_2 (
    .in0(rom_1_data[18:16]), .in1(rom_1_data[13:11]), .out(multiplexer_2_out), .sel(controlunit_1_regdst));
  Multiplexer #(.width(32), .enable("false")) multiplexer_3 (
    .in0(registerfile_1_rd2), .in1(bit_extender_1_out), .out(multiplexer_3_out), .sel(controlunit_1_alusrc));
  BitSelector #(.width(32), .group(8)) bitselector_2 (.in(bit_extender_1_out), .out(bitselector_2_out));  // open: sel
  Shifter shifter_2 (.in(bitselector_2_out), .\dist (3'b010), .out(shifter_2_out));
  ALU alu_1 (
    .F(controlunit_1_alucontrol), .B(multiplexer_3_out), .A(registerfile_1_rd1), .Y(Data_Memory),
    .ZERO(alu_1_zero));
  and and_1 (and_1_out, controlunit_1_branch, alu_1_zero);
  Adder adder_2 (.a(shifter_2_out), .b(adder_1_out), .out(adder_2_out));  // open: cin, cout

  // Notes on the sheet:
  //   PC + 4
  //   contents of rom_1 (hex, n*v repeats v):
  //   20040004 20820002 441020 10440002 2042fffd 1000fffd 20 22*0 200
  //   ADD J0 RW1 RDST0 ALUscr0 Alucon010 B0 Memwrite0 Mem2Reg0
  //   ADDI J0 RW1 RDst0 ALUscr1 ALuco010 B0 Memwrite0 Mem2Reg0
  //   Beq j0 RW0 RDst? ALUscr0, ALUcontrol 110 B1, Memwrite0 MemToreg?
endmodule

module Tests (
  output [31:0] Y,
  output [7:0] out_2,
  output [7:0] out_3,
  output [2:0] out_4
);

  BitSelector #(.width(32), .group(8)) bitselector_1 (.in(32'h12356789), .out(out_2), .sel(2'b01));
  BitSelector #(.width(32), .group(8)) bitselector_2 (.in(32'h12356789), .out(out_3), .sel(2'b01));
  BitSelector #(.group(3)) bitselector_3 (.in(out_3), .out(out_4), .sel(2'b00));

  assign Y = 32'hf4010207;

  // Notes on the sheet:
  //   binary values in Logisim. Convince yourself how the bits are displayed.
  //   Example 2: The bit selector is configured to have 32  
  //   bit group #1 (starting at index 0) is selected for the output.
  //   That is, the 8 bits 0x67 at bit indices 15..8  are sent to the output.
  //   Example 3: Now, assume that you want to extract 3 bits at   
  //   Example 1: A simple example that illustrates how 32-bit values are displayed as 
  //   input bits and 8 output bits. The parameter constant is 1, which means that   
  //   bit indices 10..8. This can be accoplished by putting two bit selecotrs in series.
endmodule

module RegisterFile (
  input  CLK,
  input  [2:0] A1,
  input  [31:0] WD3,
  input  [2:0] A2,
  input  WE3,
  input  [2:0] A3,
  output [31:0] RD1,
  output [31:0] RD2,
  output [31:0] V0
);

  wire and_1_out, and_2_out, and_3_out, and_4_out, and_5_out, and_6_out, and_7_out, and_8_out,
       decoder_1_out0, decoder_1_out1, decoder_1_out2, decoder_1_out3, decoder_1_out4, decoder_1_out5,
       decoder_1_out6, decoder_1_out7;
  wire [31:0] a0_q, a1_q, a2_q, a3_q, at_q, v1_q, Zero_q;

  Decoder #(.select(3)) decoder_1 (
    .out0(decoder_1_out0), .out1(decoder_1_out1), .out2(decoder_1_out2), .out3(decoder_1_out3),
    .out4(decoder_1_out4), .out5(decoder_1_out5), .out6(decoder_1_out6), .out7(decoder_1_out7), .sel(A3));  // open: en
  and and_1 (and_1_out, WE3, decoder_1_out0);
  and and_2 (and_2_out, WE3, decoder_1_out1);
  and and_3 (and_3_out, WE3, decoder_1_out2);
  and and_4 (and_4_out, WE3, decoder_1_out3);
  and and_5 (and_5_out, WE3, decoder_1_out4);
  and and_6 (and_6_out, WE3, decoder_1_out5);
  and and_7 (and_7_out, WE3, decoder_1_out6);
  and and_8 (and_8_out, WE3, decoder_1_out7);
  Register #(.width(32), .Select("low")) Zero (.D({32{1'b0}}), .en(and_1_out), .Q(Zero_q), .clk(CLK));  // open: clr
  Register #(.width(32), .Select("low")) at (.D(WD3), .en(and_2_out), .Q(at_q), .clk(CLK));  // open: clr
  Register #(.width(32), .Select("low")) u_v0 (.D(WD3), .en(and_3_out), .Q(V0), .clk(CLK));  // open: clr
  Register #(.width(32), .Select("low")) v1 (.D(WD3), .en(and_4_out), .Q(v1_q), .clk(CLK));  // open: clr
  Register #(.width(32), .Select("low")) a0 (.D(WD3), .en(and_5_out), .Q(a0_q), .clk(CLK));  // open: clr
  Register #(.width(32), .Select("low")) u_a1 (.D(WD3), .en(and_6_out), .Q(a1_q), .clk(CLK));  // open: clr
  Register #(.width(32), .Select("low")) u_a2 (.D(WD3), .en(and_7_out), .Q(a2_q), .clk(CLK));  // open: clr
  Register #(.width(32), .Select("low")) u_a3 (.D(WD3), .en(and_8_out), .Q(a3_q), .clk(CLK));  // open: clr
  Multiplexer #(.select(3), .width(32)) multiplexer_1 (
    .in0(Zero_q), .in1(at_q), .in2(V0), .in3(v1_q), .in4(a0_q), .in5(a1_q), .in6(a2_q), .in7(a3_q),
    .out(RD1), .sel(A1));  // open: en
  Multiplexer #(.select(3), .width(32)) multiplexer_2 (
    .in0(Zero_q), .in1(at_q), .in2(V0), .in3(v1_q), .in4(a0_q), .in5(a1_q), .in6(a2_q), .in7(a3_q),
    .out(RD2), .sel(A2));  // open: en

  // Notes on the sheet:
  //   Writedata
  //   WriteRegister
  //   Read register1
  //   Readdata
  //   WE-->
  //   Regwrite bestämmer om 
  //   operation ska lagras i register eller ej
endmodule

module ControlUnit (
  input  [31:0] Instruction,
  output RegDst,
  output RegWrite,
  output ALUSrc,
  output [2:0] ALUControl,
  output Branch
);

  wire comparator_4_eq;
  wire [2:0] multiplexer_1_out;
  wire [5:0] bitselector_1_out;
  wire [31:0] shifter_1_out;

  Shifter #(.width(32), .shift("lr")) shifter_1 (.in(Instruction), .\dist (5'b11010), .out(shifter_1_out));
  BitSelector #(.width(32), .group(6)) bitselector_1 (.in(shifter_1_out), .out(bitselector_1_out), .sel(3'b000));
  Comparator #(.width(6), .mode("unsigned")) comparator_1 (
    .a(bitselector_1_out), .b(6'b001000), .eq(ALUSrc));  // open: gt, lt
  Comparator #(.width(6), .mode("unsigned")) comparator_2 (
    .a(bitselector_1_out), .b({6{1'b0}}), .eq(RegDst));  // open: gt, lt
  Comparator #(.width(6), .mode("unsigned")) comparator_3 (
    .a(bitselector_1_out), .b(6'b000100), .eq(Branch));  // open: gt, lt
  Comparator #(.width(6), .mode("unsigned")) comparator_4 (
    .a(bitselector_1_out), .b(6'b010001), .eq(comparator_4_eq));  // open: gt, lt
  Multiplexer #(.width(3), .enable("false")) multiplexer_1 (
    .in0(3'b010), .in1(3'b110), .out(multiplexer_1_out), .sel(Branch));
  or or_1 (RegWrite, ALUSrc, RegDst);
  Multiplexer #(.width(3), .enable("false")) multiplexer_2 (
    .in0(multiplexer_1_out), .in1(3'b011), .out(ALUControl), .sel(comparator_4_eq));

  // Notes on the sheet:
  //   Shifting 26bits right to get the opcode as the LSB
  //   ADD rd,dr,rt--> 000000 rs rt rd 00000 10000 
  //   ADDI rt,rs,imm--> 001000 rs rt imm
  //   select takes OP as input
  //   Addi?
  //   jump
  //   If opcode = 0 -> It is a R-type instruction
  //   BLZT
  //   Om ALUscr(0): R-type
  //   Om Aluscr(1)=I-type
  //   010 A+B
  //   110 A-B
  //   RegDst bestämmer vilken register som ska ta emot resultatet från en instruktion/operation för att lagra.
  //   RegWrite bestämmer om resultatet från en operation ska lagras i register(1) eller om det ska ignoreras(0). 
  //   R-type(Rd) 15-11
  //   I-type(rt) 20-16
endmodule
